// Logisim project processador_monocilo.circ as structural Verilog: 9 circuits, main circuit main
module main (
  input  [31:0] PC,
  input  [31:0] Inst,
  output [31:0] AtuaPC,
  output [31:0] DataReadORALUResult,
  output IfZero,
  output [31:0] out_6
);

  wire and_1_out, clock_1_out, unid_controle_1_alusrc, unid_controle_1_branch, unid_controle_1_memr,
       unid_controle_1_memtoreg, unid_controle_1_memw, unid_controle_1_regdst, unid_controle_1_regw;
  wire [1:0] unid_controle_1_aluop;
  wire [2:0] ALU_CONTROL_out_3;
  wire [4:0] multiplexer_1_out, separa_inst_1_inst_15_11, separa_inst_1_inst_20_16, separa_inst_1_inst_25_21;
  wire [5:0] separa_inst_1_inst_5_0, separa_inst_1_inst_31_26;
  wire [15:0] separa_inst_1_inst_15_0;
  wire [31:0] adder_1_out, adder_2_out, banco_regis_1_readdata1_2, banco_regis_1_readdata2,
       extensor_1_inst32bit, mem_dados_1_out_6, multiplexer_2_out, shifter_1_out;

  separa_inst separa_inst_1 (
    .Inst_31_0(Inst), .Inst_31_26(separa_inst_1_inst_31_26), .Inst_25_21(separa_inst_1_inst_25_21),
    .Inst_20_16(separa_inst_1_inst_20_16), .Inst_15_11(separa_inst_1_inst_15_11),
    .Inst_15_0(separa_inst_1_inst_15_0), .Inst_5_0(separa_inst_1_inst_5_0));
  Adder #(.width(32)) adder_1 (.a(PC), .b(32'h4), .out(adder_1_out));  // open: cin, cout
  Multiplexer #(.width(5), .enable("false")) multiplexer_1 (
    .in0(separa_inst_1_inst_20_16), .in1(separa_inst_1_inst_15_11), .out(multiplexer_1_out),
    .sel(unid_controle_1_regdst));
  unid_controle unid_controle_1 (
    .in_1(separa_inst_1_inst_31_26), .RegDst(unid_controle_1_regdst), .RegW(unid_controle_1_regw),
    .ALUOp(unid_controle_1_aluop), .MemToReg(unid_controle_1_memtoreg), .MemR(unid_controle_1_memr),
    .ALUSrc(unid_controle_1_alusrc), .MemW(unid_controle_1_memw), .Branch(unid_controle_1_branch));
  banco_regis banco_regis_1 (
    .RegW(unid_controle_1_regw), .ReadData1(separa_inst_1_inst_25_21), .ReadReg2(separa_inst_1_inst_20_16),
    .ReadData1_2(banco_regis_1_readdata1_2), .ReadData2(banco_regis_1_readdata2), .WriteReg(multiplexer_1_out));  // open: WriteData
  extensor extensor_1 (.Inst_15_0(separa_inst_1_inst_15_0), .Inst32bit(extensor_1_inst32bit));
  Shifter #(.width(32)) shifter_1 (.in(extensor_1_inst32bit), .\dist (5'b00010), .out(shifter_1_out));
  // Probe on unid_controle_1_alusrc
  // Probe on unid_controle_1_aluop
  Adder #(.width(32)) adder_2 (.a(adder_1_out), .b(shifter_1_out), .out(adder_2_out));  // open: cin, cout
  Multiplexer #(.width(32), .enable("false")) multiplexer_2 (
    .in0(banco_regis_1_readdata2), .in1(extensor_1_inst32bit), .out(multiplexer_2_out),
    .sel(unid_controle_1_alusrc));
  controle_ula ALU_CONTROL (.in_1(unid_controle_1_aluop), .in_2(separa_inst_1_inst_5_0), .out_3(ALU_CONTROL_out_3));
  Multiplexer #(.width(32), .enable("false")) multiplexer_3 (
    .in0(adder_1_out), .in1(adder_2_out), .out(AtuaPC), .sel(and_1_out));
  and and_1 (and_1_out, unid_controle_1_branch, IfZero);
  // Probe on multiplexer_2_out
  Clock clock_1 (.out(clock_1_out));
  ula ALU (
    .out_6(IfZero), .in_1(banco_regis_1_readdata1_2), .in_4(multiplexer_2_out), .in_3(ALU_CONTROL_out_3),
    .in_2(clock_1_out), .out_5(out_6));
  // Probe on ALU_CONTROL_out_3
  mem_dados mem_dados_1 (
    .MemW(unid_controle_1_memw), .MemR(unid_controle_1_memtoreg), .ALUResult(out_6),
    .ReadData2(banco_regis_1_readdata2), .in_5(clock_1_out), .out_6(mem_dados_1_out_6));
  Multiplexer #(.width(32), .enable("false")) multiplexer_4 (
    .in0(mem_dados_1_out_6), .in1(out_6), .out(DataReadORALUResult), .sel(unid_controle_1_memr));
  // Probe on unid_controle_1_memr
endmodule

module ula (
  input  [31:0] in_1,
  input  in_2,
  input  [2:0] in_3,
  input  [31:0] in_4,
  output [31:0] out_5,
  output out_6
);

  wire or_2_out;
  wire [31:0] adder_1_out, and_1_out, multiplexer_1_out, or_1_out, subtractor_1_out;

  Multiplier multiplier_1 ();  // open: a, b, out, cin, cout
  Adder #(.width(32)) adder_1 (.a(in_1), .b(in_4), .out(adder_1_out));  // open: cin, cout
  Subtractor #(.width(32)) subtractor_1 (.a(in_1), .b(in_4), .out(subtractor_1_out));  // open: bin, bout
  assign and_1_out = in_1 & in_4;  // AND_Gate and_1, 32 bits wide
  assign or_1_out = in_1 | in_4;  // OR_Gate or_1, 32 bits wide
  Multiplexer #(.select(3), .width(32), .enable("false")) multiplexer_1 (
    .in0(adder_1_out), .in1(subtractor_1_out), .in2(in_1), .in3(and_1_out), .in4(or_1_out),
    .out(multiplexer_1_out), .sel(in_3));  // open: in5, in6, in7
  not not_1 (out_6, or_2_out);
  or or_2 (or_2_out, multiplexer_1_out[0], multiplexer_1_out[1], multiplexer_1_out[2], multiplexer_1_out[3], multiplexer_1_out[4], multiplexer_1_out[5], multiplexer_1_out[6], multiplexer_1_out[7], multiplexer_1_out[8], multiplexer_1_out[9], multiplexer_1_out[10], multiplexer_1_out[11], multiplexer_1_out[12], multiplexer_1_out[13], multiplexer_1_out[14], multiplexer_1_out[15], multiplexer_1_out[16], multiplexer_1_out[17], multiplexer_1_out[18], multiplexer_1_out[19], multiplexer_1_out[20], multiplexer_1_out[21], multiplexer_1_out[22], multiplexer_1_out[23], multiplexer_1_out[24], multiplexer_1_out[25], multiplexer_1_out[26], multiplexer_1_out[27], multiplexer_1_out[28], multiplexer_1_out[29], multiplexer_1_out[30], multiplexer_1_out[31]);
  RAM #(.dataWidth(32), .databus("bibus")) ram_1 (
    .addr({8{1'b0}}), .we(1'b1), .oe(in_2), .clk(in_2), .din(multiplexer_1_out), .dout(out_5));
endmodule

module controle_ula (
  input  [1:0] in_1,
  input  [5:0] in_2,
  output [2:0] out_3
);

  wire add_out, beq_out, ls_out, rformat_out, sub_out;
  wire [2:0] and_2_out, and_3_out, and_4_out, and_5_out, and_6_out;
  wire [2:2] and_out, mult_out, or_2_out, or_3_out, or_out;

  and add (add_out, rformat_out, ~in_2[0], ~in_2[1], ~in_2[2], ~in_2[4], ~in_2[4], in_2[5]);  // AND_Gate
  and sub (sub_out, rformat_out, ~in_2[0], in_2[1], ~in_2[2], ~in_2[4], ~in_2[4], in_2[5]);  // AND_Gate
  and mult (mult_out[2], rformat_out, ~in_2[0], ~in_2[1], ~in_2[2], in_2[4], in_2[4], ~in_2[5]);  // AND_Gate
  and \and  (and_out[2], rformat_out, ~in_2[0], ~in_2[1], in_2[2], ~in_2[4], ~in_2[4], in_2[5]);  // AND_Gate
  and \or  (or_out[2], rformat_out, in_2[0], ~in_2[1], in_2[2], ~in_2[4], ~in_2[4], in_2[5]);  // AND_Gate
  and rformat (rformat_out, ~in_1[0], in_1[1]);  // AND_Gate
  and ls (ls_out, ~in_1[0], ~in_1[1]);  // AND_Gate
  and beq (beq_out, in_1[0], ~in_1[1]);  // AND_Gate
  or or_2 (or_2_out[2], ls_out, add_out);
  or or_3 (or_3_out[2], beq_out, sub_out);
  // Probe on 3'b000
  // Probe on {3{or_2_out[2]}}
  // Probe on {3{or_3_out[2]}}
  assign and_2_out = 3'b011 & {3{and_out[2]}};  // AND_Gate and_2, 3 bits wide
  assign and_3_out = 3'b100 & {3{or_out[2]}};  // AND_Gate and_3, 3 bits wide
  // Probe on 3'b001
  // Probe on and_4_out
  assign and_4_out = 3'b000 & {3{or_2_out[2]}};  // AND_Gate and_4, 3 bits wide
  assign and_5_out = 3'b001 & {3{or_3_out[2]}};  // AND_Gate and_5, 3 bits wide
  assign and_6_out = 3'b010 & {3{mult_out[2]}};  // AND_Gate and_6, 3 bits wide
  assign out_3 = and_4_out | and_5_out | and_6_out | and_2_out | and_3_out;  // OR_Gate or_4, 3 bits wide

  assign in_2[3] = in_2[4];
endmodule

// ControlUnit
module unid_controle (
  input  [5:0] in_1,
  output RegDst,
  output RegW,
  output [1:0] ALUOp,
  output MemToReg,
  output MemR,
  output ALUSrc,
  output MemW,
  output Branch
);

  and rformat (ALUOp[1], ~in_1[0], ~in_1[1], ~in_1[2], ~in_1[3], ~in_1[4], ~in_1[5]);  // AND_Gate
  and lw (MemR, in_1[0], ~in_1[1], ~in_1[2], ~in_1[3], in_1[4], in_1[5]);  // AND_Gate
  and sw (MemW, in_1[0], ~in_1[1], in_1[2], ~in_1[3], in_1[4], in_1[5]);  // AND_Gate
  and beq (ALUOp[0], ~in_1[0], ~in_1[1], ~in_1[2], in_1[3], ~in_1[4], ~in_1[5]);  // AND_Gate
  or or_1 (RegW, ALUOp[1], MemR);
  or or_2 (ALUSrc, MemR, MemW);

  assign Branch = ALUOp[0];
  assign MemToReg = MemR;
  assign RegDst = ALUOp[1];
endmodule

// DataMem
module mem_dados (
  input  MemW,
  input  MemR,
  input  [31:0] ALUResult,
  input  [31:0] ReadData2,
  input  in_5,
  output [31:0] out_6
);

  RAM #(.addrWidth(24), .dataWidth(32), .databus("bibus")) ram_1 (
    .addr(ALUResult[23:0]), .we(MemW), .oe(MemR), .clk(in_5), .din(ReadData2), .dout(out_6));

  assign ALUResult[30:24] = {7{ALUResult[31]}};
  // also tied to GND on the sheet: ALUResult[31]
endmodule

// Reg
module banco_regis (
  input  RegW,
  input  [4:0] ReadData1,
  input  [4:0] ReadReg2,
  input  [4:0] WriteReg,
  input  [31:0] WriteData,
  output [31:0] ReadData1_2,
  output [31:0] ReadData2
);

  wire and_1_out, and_2_out, and_3_out, and_4_out, and_5_out, and_6_out, and_7_out, and_8_out, and_9_out,
       and_10_out, and_11_out, and_12_out, and_13_out, and_14_out, and_15_out, and_16_out, and_17_out,
       and_18_out, and_19_out, and_20_out, and_21_out, and_22_out, and_23_out, and_24_out, and_26_out,
       and_28_out, and_29_out, and_30_out, and_31_out, and_32_out, clock_1_out, decoder_1_out0,
       decoder_1_out1, decoder_1_out2, decoder_1_out3, decoder_1_out4, decoder_1_out5, decoder_1_out6,
       decoder_1_out7, decoder_1_out8, decoder_1_out9, decoder_1_out10, decoder_1_out11, decoder_1_out12,
       decoder_1_out13, decoder_1_out14, decoder_1_out15, decoder_1_out17, decoder_1_out18, decoder_1_out19,
       decoder_1_out20, decoder_1_out21, decoder_1_out22, decoder_1_out23, decoder_1_out24, decoder_1_out25,
       decoder_1_out26, decoder_1_out27, decoder_1_out28, decoder_1_out29, decoder_1_out30, decoder_1_out31,
       decoder_2_out0, decoder_2_out1, undriven_4;
  wire [31:0] register_1_q, register_2_q, register_3_q, register_4_q, register_5_q, register_6_q,
       register_7_q, register_8_q, register_9_q, register_10_q, register_11_q, register_12_q, register_13_q,
       register_14_q, register_15_q, register_16_q, register_17_q, register_18_q, register_19_q,
       register_20_q, register_21_q, register_22_q, register_23_q, register_24_q, register_25_q,
       register_26_q, register_27_q, register_28_q, register_29_q, register_30_q, register_31_q,
       register_32_q, undriven, undriven_2, undriven_3;

  Clock clock_1 (.out(clock_1_out));
  Decoder #(.select(5), .enable("false")) decoder_1 (
    .out0(decoder_1_out0), .out1(decoder_1_out1), .out2(decoder_1_out2), .out3(decoder_1_out3),
    .out4(decoder_1_out4), .out5(decoder_1_out5), .out6(decoder_1_out6), .out7(decoder_1_out7),
    .out8(decoder_1_out8), .out9(decoder_1_out9), .out10(decoder_1_out10), .out11(decoder_1_out11),
    .out12(decoder_1_out12), .out13(decoder_1_out13), .out14(decoder_1_out14), .out15(decoder_1_out15),
    .out16(decoder_1_out15), .out17(decoder_1_out17), .out18(decoder_1_out18), .out19(decoder_1_out19),
    .out20(decoder_1_out20), .out21(decoder_1_out21), .out22(decoder_1_out22), .out23(decoder_1_out23),
    .out24(decoder_1_out24), .out25(decoder_1_out25), .out26(decoder_1_out26), .out27(decoder_1_out27),
    .out28(decoder_1_out28), .out29(decoder_1_out29), .out30(decoder_1_out30), .out31(decoder_1_out31),
    .sel(WriteReg));
  Decoder #(.tristate("true"), .enable("false")) decoder_2 (.out0(decoder_2_out0), .out1(decoder_2_out1), .sel(RegW));
  Register #(.width(32)) register_1 (.D(WriteData), .en(and_1_out), .clk(clock_1_out), .Q(register_1_q));  // open: clr
  and and_1 (and_1_out, decoder_1_out0, decoder_2_out1);
  Register #(.width(32)) register_2 (.D(undriven_2), .en(and_2_out), .clk(clock_1_out), .Q(register_2_q));  // open: clr
  and and_2 (and_2_out, decoder_1_out8, decoder_2_out1);
  Register #(.width(32)) register_3 (.D(undriven_3), .en(and_3_out), .clk(clock_1_out), .Q(register_3_q));  // open: clr
  and and_3 (and_3_out, decoder_1_out15, undriven_4);
  Register #(.width(32)) register_4 (.D(undriven), .en(and_4_out), .clk(clock_1_out), .Q(register_4_q));  // open: clr
  and and_4 (and_4_out, decoder_1_out24, undriven_4);
  Register #(.width(32)) register_5 (.D(WriteData), .en(and_5_out), .clk(clock_1_out), .Q(register_5_q));  // open: clr
  and and_5 (and_5_out, decoder_1_out1, decoder_2_out1);
  Register #(.width(32)) register_6 (.D(undriven_2), .en(and_6_out), .clk(clock_1_out), .Q(register_6_q));  // open: clr
  and and_6 (and_6_out, decoder_1_out9, decoder_2_out1);
  Register #(.width(32)) register_7 (.D(undriven_3), .en(and_7_out), .clk(clock_1_out), .Q(register_7_q));  // open: clr
  and and_7 (and_7_out, decoder_1_out17, undriven_4);
  Register #(.width(32)) register_8 (.D(undriven), .en(and_8_out), .clk(clock_1_out), .Q(register_8_q));  // open: clr
  and and_8 (and_8_out, decoder_1_out25, undriven_4);
  and and_9 (and_9_out, decoder_1_out2, decoder_2_out1);
  and and_10 (and_10_out, decoder_1_out10, decoder_2_out1);
  and and_11 (and_11_out, decoder_1_out18, undriven_4);
  Register #(.width(32)) register_9 (.D(undriven), .en(and_12_out), .clk(clock_1_out), .Q(register_9_q));  // open: clr
  and and_12 (and_12_out, decoder_1_out26, undriven_4);
  Register #(.width(32)) register_10 (
    .D(WriteData), .en(and_9_out), .clk(clock_1_out), .Q(register_10_q));  // open: clr
  Register #(.width(32)) register_11 (
    .D(undriven_2), .en(and_10_out), .clk(clock_1_out), .Q(register_11_q));  // open: clr
  Register #(.width(32)) register_12 (
    .D(undriven_3), .en(and_11_out), .clk(clock_1_out), .Q(register_12_q));  // open: clr
  and and_13 (and_13_out, decoder_1_out27, undriven_4);
  Register #(.width(32)) register_13 (
    .D(WriteData), .en(and_14_out), .clk(clock_1_out), .Q(register_13_q));  // open: clr
  and and_14 (and_14_out, decoder_1_out3, decoder_2_out1);
  Register #(.width(32)) register_14 (
    .D(undriven_2), .en(and_15_out), .clk(clock_1_out), .Q(register_14_q));  // open: clr
  and and_15 (and_15_out, decoder_1_out11, decoder_2_out1);
  Register #(.width(32)) register_15 (
    .D(undriven_3), .en(and_16_out), .clk(clock_1_out), .Q(register_15_q));  // open: clr
  and and_16 (and_16_out, decoder_1_out19, undriven_4);
  Register #(.width(32)) register_16 (
    .D(undriven), .en(and_13_out), .clk(clock_1_out), .Q(register_16_q));  // open: clr
  Register #(.width(32)) register_17 (
    .D(WriteData), .en(and_17_out), .clk(clock_1_out), .Q(register_17_q));  // open: clr
  and and_17 (and_17_out, decoder_1_out4, decoder_2_out1);
  Register #(.width(32)) register_18 (
    .D(undriven_2), .en(and_18_out), .clk(clock_1_out), .Q(register_18_q));  // open: clr
  and and_18 (and_18_out, decoder_1_out12, decoder_2_out1);
  Register #(.width(32)) register_19 (
    .D(undriven_3), .en(and_19_out), .clk(clock_1_out), .Q(register_19_q));  // open: clr
  and and_19 (and_19_out, decoder_1_out20, undriven_4);
  Register #(.width(32)) register_20 (
    .D(undriven), .en(and_20_out), .clk(clock_1_out), .Q(register_20_q));  // open: clr
  and and_20 (and_20_out, decoder_1_out28, undriven_4);
  and and_21 (and_21_out, decoder_1_out5, decoder_2_out1);
  Register #(.width(32)) register_21 (
    .D(undriven_2), .en(and_22_out), .clk(clock_1_out), .Q(register_21_q));  // open: clr
  and and_22 (and_22_out, decoder_1_out13, decoder_2_out1);
  Register #(.width(32)) register_22 (
    .D(undriven_3), .en(and_23_out), .clk(clock_1_out), .Q(register_22_q));  // open: clr
  and and_23 (and_23_out, decoder_1_out21, undriven_4);
  Register #(.width(32)) register_23 (
    .D(undriven), .en(and_24_out), .clk(clock_1_out), .Q(register_23_q));  // open: clr
  and and_24 (and_24_out, decoder_1_out29, undriven_4);
  Register #(.width(32)) register_24 (
    .D(WriteData), .en(and_21_out), .clk(clock_1_out), .Q(register_24_q));  // open: clr
  and and_25 (clock_1_out, decoder_1_out30, undriven_4);
  Register #(.width(32)) register_25 (
    .D(WriteData), .en(and_26_out), .clk(clock_1_out), .Q(register_25_q));  // open: clr
  and and_26 (and_26_out, decoder_1_out6, decoder_2_out1);
  Register #(.width(32)) register_26 (
    .D(undriven_2), .en(clock_1_out), .clk(clock_1_out), .Q(register_26_q));  // open: clr
  and and_27 (clock_1_out, decoder_1_out14, decoder_2_out1);
  Register #(.width(32)) register_27 (
    .D(undriven_3), .en(and_28_out), .clk(clock_1_out), .Q(register_27_q));  // open: clr
  and and_28 (and_28_out, decoder_1_out22, undriven_4);
  Register #(.width(32)) register_28 (
    .D(undriven), .en(clock_1_out), .clk(clock_1_out), .Q(register_28_q));  // open: clr
  Register #(.width(32)) register_29 (
    .D(WriteData), .en(and_29_out), .clk(clock_1_out), .Q(register_29_q));  // open: clr
  and and_29 (and_29_out, decoder_1_out7, decoder_2_out1);
  Register #(.width(32)) register_30 (
    .D(undriven_2), .en(and_30_out), .clk(clock_1_out), .Q(register_30_q));  // open: clr
  and and_30 (and_30_out, decoder_1_out15, decoder_2_out1);
  Register #(.width(32)) register_31 (
    .D(undriven_3), .en(and_31_out), .clk(clock_1_out), .Q(register_31_q));  // open: clr
  and and_31 (and_31_out, decoder_1_out23, undriven_4);
  Register #(.width(32)) register_32 (
    .D(undriven), .en(and_32_out), .clk(clock_1_out), .Q(register_32_q));  // open: clr
  and and_32 (and_32_out, decoder_1_out31, undriven_4);
  Multiplexer #(.select(5), .width(32)) multiplexer_1 (
    .in0(register_1_q), .in1(register_5_q), .in2(register_10_q), .in3(register_13_q), .in4(register_17_q),
    .in5(register_24_q), .in6(register_25_q), .in7(register_29_q), .in8(register_2_q), .in9(register_6_q),
    .in10(register_11_q), .in11(register_14_q), .in12(register_18_q), .in13(register_21_q),
    .in14(register_26_q), .in15(register_30_q), .in16(register_3_q), .in17(register_7_q),
    .in18(register_12_q), .in19(register_15_q), .in20(register_19_q), .in21(register_22_q),
    .in22(register_27_q), .in23(register_31_q), .in24(register_4_q), .in25(register_8_q),
    .in26(register_9_q), .in27(register_16_q), .in28(register_20_q), .in29(register_23_q),
    .in30(register_28_q), .in31(register_32_q), .out(ReadData1_2), .sel(ReadData1), .en(decoder_2_out0));
  Multiplexer #(.select(5), .width(32)) multiplexer_2 (
    .in0(register_1_q), .in1(register_5_q), .in2(register_10_q), .in3(register_13_q), .in4(register_17_q),
    .in5(register_24_q), .in6(register_25_q), .in7(register_29_q), .in8(register_2_q), .in9(register_6_q),
    .in10(register_11_q), .in11(register_14_q), .in12(register_18_q), .in13(register_21_q),
    .in14(register_26_q), .in15(register_30_q), .in16(register_3_q), .in17(register_7_q),
    .in18(register_12_q), .in19(register_15_q), .in20(register_19_q), .in21(register_22_q),
    .in22(register_27_q), .in23(register_31_q), .in24(register_4_q), .in25(register_8_q),
    .in26(register_9_q), .in27(register_16_q), .in28(register_20_q), .in29(register_23_q),
    .in30(register_28_q), .in31(register_32_q), .out(ReadData2), .sel(ReadReg2), .en(decoder_2_out0));
endmodule

// SEx
module extensor (
  input  [15:0] Inst_15_0,
  output [31:0] Inst32bit
);


  assign Inst32bit = {{17{Inst_15_0[15]}}, Inst_15_0[14:0]};
endmodule

module controle_PC (
  input  AtuaPC,
  input  [31:0] ALUResult,
  input  ZB,
  input  JUMP,
  input  [31:0] InstAtual,
  output [31:0] PC
);

  wire clock_1_out;
  wire [31:0] adder_1_out, adder_2_out, multiplexer_1_out, multiplexer_2_out;

  Register #(.width(32)) register_1 (.D(multiplexer_2_out), .en(AtuaPC), .clk(clock_1_out), .Q(PC));  // open: clr
  Clock clock_1 (.out(clock_1_out));
  Adder #(.width(32)) adder_1 (.a(32'h1), .b(PC), .out(adder_1_out));  // open: cin, cout
  Adder #(.width(32)) adder_2 (.a(adder_1_out), .b(ALUResult), .out(adder_2_out));  // open: cin, cout
  Multiplexer #(.width(32), .enable("false")) multiplexer_1 (
    .in0(adder_1_out), .in1(adder_2_out), .out(multiplexer_1_out), .sel(ZB));
  Multiplexer #(.width(32), .enable("false")) multiplexer_2 (
    .in0(multiplexer_1_out), .in1({2'b00, adder_1_out[31:28], InstAtual[25:0]}), .out(multiplexer_2_out),
    .sel(JUMP));
endmodule

module separa_inst (
  input  [31:0] Inst_31_0,
  output [5:0] Inst_31_26,
  output [4:0] Inst_25_21,
  output [4:0] Inst_20_16,
  output [4:0] Inst_15_11,
  output [15:0] Inst_15_0,
  output [5:0] Inst_5_0
);


  assign Inst_5_0 = Inst_31_0[5:0];
  assign Inst_15_0 = Inst_31_0[15:0];
  assign Inst_15_11 = Inst_31_0[15:11];
  assign Inst_20_16 = Inst_31_0[20:16];
  assign Inst_25_21 = Inst_31_0[25:21];
  assign Inst_31_26 = Inst_31_0[31:26];
endmodule
